# Fritzing sketch NEOPIXEL_RING_SKETCH (saved by Fritzing 0.9.3b)
breadboards: 1

parts:
  Componente1 = 12 NeoPixel Ring [part_number=1643]
  Componente2 = Arduino Nano (Rev3.0)

nets:
  N1: Componente1.IN, Componente2.D1/TX
  VDD: Componente1.VDD, Componente2.5V
  GND: Componente1.GND, Componente2.GND

custom parts:
  12 NeoPixel Ring: 12 ultra bright smart LED NeoPixels are arranged in a circle with 1.5" (37mm) outer diameter. The rings are 'chainable' - connect the output pin of one to the input pin of another. Use only one microcontroller pin to control as many as you can chain together! Each LED is addressable as the driver chip is inside the LED. Each one has ~18mA constant current drive so the color will be very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
